# Fritzing sketch BallInTorus_FritzingSchematics (saved by Fritzing 0.9.5d)
breadboards: 1

parts:
  Part1 = 24 NeoPixel Ring [part_number=1586]
  Part2 = Arduino Uno (Rev3) - ICSP
  Part3 = InvenSense MPU6050
  BAT1 = BC9VPC [package=bc9vpc]  # not connected

nets:
  N1: Part1.IN, Part2.D6_PWM
  VDD: Part1.VDD, Part2.5V, Part3.VCC
  GND: Part1.GND, Part2.GND, Part3.GND, Part3.AD0
  N2: Part2.A4/SDA, Part3.SDA
  N3: Part2.A5/SCL, Part3.SCL
  N4: Part2.D2, Part3.INT

notes:
  IN pin is in the direction of the MPU X axis

custom parts:
  24 NeoPixel Ring: 24 ultra bright smart LED NeoPixels are arranged in a circle with 2.6" (66mm) outer diameter. The rings are 'chainable' - connect the output pin of one to the input pin of another. Use only one microcontroller pin to control as many as you can chain together! Each LED is addressable as the driver chip is inside the LED. Each one has ~18mA constant current drive so the color will be very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
